// Logisim project Proj.circ as structural Verilog: 2 circuits, main circuit main
module main (
);

  wire _0, _1, _2, _3, _4, _5, _6, _7, _8, _9, bit_extender_1_out, bit_extender_2_out, bit_extender_3_out,
       bit_extender_4_out, bit_extender_5_out, bit_extender_6_out, CLEAR_out, not_1_out, or_5_out;
  wire [3:0] counter_1_q, demultiplexer_1_out1, demultiplexer_1_out2, demultiplexer_1_out3,
       demultiplexer_1_out4, demultiplexer_1_out5, demultiplexer_1_out6, or_1_out, ram_1_data, register_1_q,
       register_2_q, undriven, undriven_2, undriven_3, undriven_4, undriven_5, undriven_6;

  or or_1 (or_1_out[0], _1, _3, _5, _7, _9);
  or or_2 (or_1_out[1], _2, _3, _6, _7);
  or or_3 (or_1_out[2], _4, _5, _6, _7);
  or or_4 (or_1_out[3], _8, _9);
  Counter #(.width(4), .max('h6), .ongoal("load")) counter_1 (
    .Q(counter_1_q), .clk(or_5_out), .clr(CLEAR_out));  // open: load, D, count, carry
  or or_5 (or_5_out, _0, or_1_out[0], or_1_out[1], or_1_out[2], or_1_out[3]);
  _4bit_Latch u_4bit_latch_1 ();  // open: out_5, in_1, in_3, in_4, in_2
  not not_1 (not_1_out, or_5_out);
  Register #(.width(4), .trigger("high")) register_1 (.D(or_1_out), .Q(register_1_q), .clk(or_5_out));  // open: en, clr
  RAM #(.addrWidth(4), .dataWidth(4), .bus("separate")) ram_1 (
    .addr(counter_1_q), .din(register_1_q), .data(ram_1_data), .clk(not_1_out), .clr(CLEAR_out));  // open: str, sel, ld
  Register #(.width(4), .trigger("high")) register_2 (
    .D(ram_1_data), .Q(register_2_q), .clk(not_1_out));  // open: en, clr
  Demultiplexer #(.select(4), .width(4)) demultiplexer_1 (
    .out1(demultiplexer_1_out1), .out2(demultiplexer_1_out2), .out3(demultiplexer_1_out3),
    .out4(demultiplexer_1_out4), .out5(demultiplexer_1_out5), .out6(demultiplexer_1_out6), .in(register_2_q),
    .sel(counter_1_q));  // open: out0, out7, out8, out9, out10, out11, out12, out13, out14, out15, en
  Button CLEAR (.out(CLEAR_out));
  Hex_Digit_Display hex_digit_display_1 (.value(undriven_2));  // open: dp
  Hex_Digit_Display hex_digit_display_2 (.value(undriven));  // open: dp
  Bit_Extender #(.in_width(4), .out_width(1)) bit_extender_1 (.in(demultiplexer_1_out1), .out(bit_extender_1_out));
  Bit_Extender #(.in_width(4), .out_width(1)) bit_extender_2 (.in(demultiplexer_1_out2), .out(bit_extender_2_out));
  Hex_Digit_Display hex_digit_display_3 (.value(undriven_3));  // open: dp
  Hex_Digit_Display hex_digit_display_4 (.value(undriven_4));  // open: dp
  Bit_Extender #(.in_width(4), .out_width(1)) bit_extender_3 (.in(demultiplexer_1_out3), .out(bit_extender_3_out));
  Button u__2 (.out(_2));
  Button u__1 (.out(_1));
  Button u__4 (.out(_4));
  Button u__5 (.out(_5));
  Button u__7 (.out(_7));
  Button u__8 (.out(_8));
  Button u__0 (.out(_0));
  Hex_Digit_Display hex_digit_display_5 (.value(undriven_5));  // open: dp
  Bit_Extender #(.in_width(4), .out_width(1)) bit_extender_4 (.in(demultiplexer_1_out4), .out(bit_extender_4_out));
  Bit_Extender #(.in_width(4), .out_width(1)) bit_extender_5 (.in(demultiplexer_1_out5), .out(bit_extender_5_out));
  Button u__3 (.out(_3));
  Button u__6 (.out(_6));
  Button u__9 (.out(_9));
  Hex_Digit_Display hex_digit_display_6 (.value(undriven_6));  // open: dp
  Bit_Extender #(.in_width(4), .out_width(1)) bit_extender_6 (.in(demultiplexer_1_out6), .out(bit_extender_6_out));
endmodule

module _4bit_Latch (
  input  [3:0] in_1,
  input  in_2,
  input  in_3,
  input  [3:0] in_4,
  output out_5
);

  wire and_1_out, and_2_out, nor_2_out, not_1_out;

  not not_1 (not_1_out, in_3);
  and and_1 (and_1_out, not_1_out, in_2);
  and and_2 (and_2_out, in_3, in_2);
  nor nor_1 (out_5, and_1_out, nor_2_out);
  nor nor_2 (nor_2_out, out_5, and_2_out);
endmodule
